// Digital circuit blinkenlights.dig as structural Verilog
module blinkenlights (
  input  CLOCK,
  input  RED,
  input  BLINK,
  input  GREEN
);

  wire nand_1_out, nand_2_out, nand_3_out, not_1_out, not_2_out;

  nand nand_1 (nand_1_out, CLOCK, BLINK);
  nand nand_2 (nand_2_out, nand_1_out, GREEN);
  nand nand_3 (nand_3_out, RED, RED);
  not not_1 (not_1_out, nand_2_out);
  not not_2 (not_2_out, nand_3_out);
  LED TESTING___GOOD (.in(not_1_out));
  LED ERROR (.in(not_2_out));

  // Notes on the sheet:
  //   CLOCK: Hz: 2
  //   BLINK\_CLOCK
endmodule
